// Logisim project Project1Given.circ as structural Verilog: 4 circuits, main circuit main
module main (
  input  in_1,
  input  in_2,
  input  in_3,
  input  in_4,
  input  Five,
  output N,
  output E,
  output [3:0] out_8
);

  wire fiveseven_1_a, fiveseven_1_b, fiveseven_1_c, fiveseven_1_d, fiveseven_1_e, fiveseven_1_f,
       fiveseven_1_g;

  Compare compare_1 (.X0(1'b1), .Y0(1'b1), .X1(1'b1), .Y1(1'b1), .X2(1'b0), .Y2(1'b0), .N(N), .E(E));
  Gray gray_1 (.B0(1'b1), .B1(1'b0), .B2(1'b1), .B3(1'b0), .G0(out_8[0]), .G3(out_8[1]), .G1(out_8[2]), .G2(out_8[3]));
  FiveSeven fiveseven_1 (
    .V(in_1), .W(in_2), .X(in_3), .Y(in_4), .Z(Five), .A(fiveseven_1_a), .B(fiveseven_1_b),
    .C(fiveseven_1_c), .D(fiveseven_1_d), .E(fiveseven_1_e), .F(fiveseven_1_f), .G(fiveseven_1_g));
  _7_Segment_Display u_7_segment_display_1 (
    .g(fiveseven_1_g), .f(fiveseven_1_f), .a(fiveseven_1_a), .b(fiveseven_1_b), .e(fiveseven_1_e),
    .d(fiveseven_1_d), .c(fiveseven_1_c));  // open: dp
endmodule

module Compare (
  input  X0,
  input  Y0,
  input  X1,
  input  Y1,
  input  X2,
  input  Y2,
  output N,
  output E
);

  wire c1_out, c2_out, c3_out, not_1_out, not_2_out, not_3_out, xnor_1_out, xnor_2_out, xnor_3_out;

  xnor xnor_1 (xnor_1_out, X0, Y0);
  xnor xnor_2 (xnor_2_out, X1, Y1);
  xnor xnor_3 (xnor_3_out, X2, Y2);
  and and_1 (E, xnor_1_out, xnor_2_out, xnor_3_out);
  not not_1 (not_1_out, X2);
  and c1 (c1_out, not_1_out, Y2);
  not not_2 (not_2_out, X1);
  and c2 (c2_out, not_2_out, Y1, xnor_3_out);
  not not_3 (not_3_out, X0);
  and c3 (c3_out, not_3_out, Y0, xnor_3_out, xnor_2_out);
  or or_1 (N, c3_out, c2_out, c1_out);
endmodule

module Gray (
  input  B0,
  input  B1,
  input  B2,
  input  B3,
  output G0,
  output G3,
  output G1,
  output G2
);

  wire and_1_out, and_2_out, and_3_out, g1_Gate1_out, g1_Gate2_out, g1gate1_out, g1gate2_out, g2_gate1_out,
       g2_gate2_out, g2gate2_out, g2gate3_out, g2gte1_out, g3_gate1_out, not_1_out, not_2_out, not_3_out,
       not_4_out, not_5_out, not_6_out, not_7_out, not_8_out, not_9_out, not_10_out, not_11_out, not_12_out,
       not_13_out, not_14_out, not_15_out, not_16_out, not_18_out, not_19_out, not_20_out, not_21_out,
       or_1_out, undriven, undriven_2, undriven_3, undriven_4, xor_1_out, xor_2_out;

  not not_1 (not_1_out, undriven_2);
  not not_2 (not_2_out, undriven);
  and and_1 (and_1_out, not_1_out, not_2_out, undriven_4);
  not not_3 (not_3_out, undriven_4);
  and g2_gate2 (g2_gate2_out, undriven, undriven_3, undriven_2, undriven_4);
  and g2gte1 (g2gte1_out, B3, B2, B1, B0);
  or or_1 (or_1_out, undriven, undriven_3);
  not not_4 (not_4_out, undriven_3);
  not not_5 (not_5_out, undriven);
  and g1_Gate1 (g1_Gate1_out, not_4_out, not_5_out, not_6_out);
  not not_6 (not_6_out, undriven_2);
  and g3_gate1 (g3_gate1_out, not_3_out, undriven_2);
  not not_7 (not_7_out, undriven_2);
  not not_8 (not_8_out, undriven_3);
  or g1gate1 (g1gate1_out, B0, B1);
  not not_9 (not_9_out, undriven_3);
  and and_2 (and_2_out, undriven_4, not_7_out, not_8_out);
  not not_10 (not_10_out, B0);
  not not_11 (not_11_out, B1);
  not not_12 (not_12_out, B2);
  not not_13 (not_13_out, B3);
  not not_14 (not_14_out, B2);
  xor xor_1 (xor_1_out, undriven, not_9_out);
  not not_15 (not_15_out, undriven_3);
  and g1_Gate2 (g1_Gate2_out, or_1_out, undriven_2);
  and and_3 (and_3_out, g1gate1_out, B2);
  and g1gate2 (g1gate2_out, not_10_out, not_11_out, not_12_out);
  or g2gate2 (g2gate2_out, B1, not_13_out, not_14_out);
  xor xor_2 (xor_2_out, undriven, not_15_out);
  // OR_Gate or_2 has open pins: in0=g1_Gate2_out, in1=g1_Gate1_out, out=open
  not not_16 (not_16_out, B0);
  and g2gate3 (g2gate3_out, not_16_out, g2gate2_out);
  not not_17 (G0, undriven_3);
  not not_18 (not_18_out, undriven_4);
  or or_3 (G1, and_3_out, g1gate2_out);
  // AND_Gate and_4 has open pins: in0=xor_2_out, in1=not_18_out, out=open
  or or_4 (G2, g2gte1_out, g2gate3_out);
  and g2_gate1 (g2_gate1_out, xor_1_out, not_19_out);
  not not_19 (not_19_out, undriven_4);
  // NOT_Gate not_20 has open pins: in=open, out=not_20_out
  // OR_Gate or_5 has open pins: in0=not_20_out, in1=not_21_out, out=open
  // NOT_Gate not_21 has open pins: in=open, out=not_21_out
  or or_6 (G3, and_1_out, g3_gate1_out, and_2_out);
  // OR_Gate or_7 has open pins: in0=g2_gate1_out, in1=g2_gate2_out, out=open
endmodule

module FiveSeven (
  input  V,
  input  W,
  input  X,
  input  Y,
  input  Z,
  output A,
  output B,
  output C,
  output D,
  output E,
  output F,
  output G
);
endmodule
